// Digital circuit 2- Flip Flop.dig as structural Verilog
module _2__Flip_Flop (
  input  Reset,
  input  Sinal,
  input  Reset_2,
  input  Sinal_2,
  input  Relogio__Clock,
  input  in_10,
  input  in_11,
  output Q,
  output Q_Barra,
  output Q_2,
  output Q_Barra_2,
  output out_12
);

  wire and_1_out, and_2_out, and_3_out, not_1_out;

  nor nor_1 (out_12, in_10, in_11);
  not not_1 (not_1_out, Relogio__Clock);
  and and_1 (and_1_out, not_1_out, Relogio__Clock);
  and and_2 (and_2_out, Sinal_2, and_1_out);
  and and_3 (and_3_out, and_1_out, Reset_2);
  RS_FF_AS rs_ff_as_1 (.S(and_2_out), .R(and_3_out), .Q(Q_2), .nQ(Q_Barra_2));
  nor nor_2 (Q, Reset, Q_Barra);
  nor nor_3 (Q_Barra, Q, Sinal);
endmodule
