// Digital circuit 3- Barramento.dig as structural Verilog
module _3__Barramento (
  input  A1,
  input  A0,
  input  A2,
  input  A3,
  input  Clock,
  input  D0,
  output Memory
);

  wire and_1_out, and_2_out;

  and and_1 (and_1_out, A0, ~A1, A2, A3);  // And
  and and_2 (and_2_out, and_1_out, Clock);
  D_FF d_ff_1 (.D(D0), .C(and_2_out), .Q(Memory));  // open: nQ
endmodule

/* Test case Barramento:
A3 A2 A1 A0 Clock D0 Memory
1  1  0  1    0    0   0
1  1  0  1    1    1   1
1  1  0  0    1    0   1
1  1  0  1    0    0   1
1  1  0  1    1    0   0
*/
