// Digital circuit 7- Maquina de Estado.dig as structural Verilog
module _7__Maquina_de_Estado (
  input  Temp,
  input  Clock,
  output Q0,
  output Q1
);

  wire and_1_out, and_2_out, and_3_out, d_ff_1_nq, d_ff_2_nq, or_1_out, or_2_out;

  and and_1 (and_1_out, Temp, or_1_out);
  D_FF d_ff_1 (.D(and_1_out), .C(Clock), .Q(Q1), .nQ(d_ff_1_nq));
  or or_1 (or_1_out, Q0, Q1);
  and and_2 (and_2_out, ~Temp, Q1);  // And
  and and_3 (and_3_out, Temp, d_ff_1_nq, d_ff_2_nq);
  or or_2 (or_2_out, and_2_out, and_3_out);
  D_FF d_ff_2 (.D(or_2_out), .C(Clock), .Q(Q0), .nQ(d_ff_2_nq));
endmodule
