// Digital circuit Arquivo.dig as structural Verilog
module Arquivo (
  input  Reset,
  input  Sinal,
  input  Reset_2,
  input  Sinal_2,
  input  Relogio__Clock,
  output Q,
  output Q_Barra,
  output Q_2,
  output Q_Barra_2
);

  wire and_1_out, and_2_out, and_3_out, not_1_out;

  not not_1 (not_1_out, Relogio__Clock);
  and and_1 (and_1_out, not_1_out, Relogio__Clock);
  and and_2 (and_2_out, Sinal_2, and_1_out);
  and and_3 (and_3_out, and_1_out, Reset_2);
  nor nor_1 (Q, Reset, Q_Barra);
  nor nor_2 (Q_Barra, Q, Sinal);
  RS_FF_AS rs_ff_as_1 (.S(and_2_out), .R(and_3_out), .Q(Q_2), .nQ(Q_Barra_2));
endmodule
